// Logisim project teste.circ as structural Verilog: 2 circuits, main circuit main
module main (
  input  [3:0] in_1
);

  wire pino_1_out_2, pino_1_out_3, pino_1_out_4;

  Pino pino_1 (.in_1(in_1), .out_2(pino_1_out_2), .out_3(pino_1_out_3), .out_4(pino_1_out_4));
endmodule

module Pino (
  input  [3:0] in_1,
  output out_2,
  output out_3,
  output out_4
);

  wire comparator_1_eq, comparator_2_eq, comparator_2_gt, comparator_2_lt, comparator_3_eq, comparator_3_gt,
       comparator_3_lt, or_2_out;

  Comparator #(.width(4)) comparator_1 (.a(in_1), .b(4'b0000), .eq(comparator_1_eq));  // open: gt, lt
  or or_1 (out_2, comparator_1_eq, comparator_2_gt);
  Comparator #(.width(4)) comparator_2 (
    .a(in_1), .b(4'b0101), .gt(comparator_2_gt), .eq(comparator_2_eq), .lt(comparator_2_lt));
  or or_2 (or_2_out, comparator_2_lt, comparator_2_eq);
  and and_1 (out_3, or_2_out, comparator_3_lt);
  or or_3 (out_4, comparator_3_gt, comparator_3_eq);
  Comparator #(.width(4)) comparator_3 (
    .a(in_1), .b(4'b1010), .gt(comparator_3_gt), .eq(comparator_3_eq), .lt(comparator_3_lt));
endmodule
